# Fritzing sketch ENTRADAS (saved by Fritzing 0.9.3b)
breadboards: 2

parts:
  Part1 = Arduino Nano (Rev3.0)
  R1 = Trimmer Potentiometer [maximum_resistance=10kΩ package=THT]
  R2 = Trimmer Potentiometer [maximum_resistance=10kΩ package=THT]
  S1 = Pushbutton [package="[THT]"]
  S2 = Pushbutton [package="[THT]"]
  S3 = Pushbutton [package="[THT]"]
  S4 = Pushbutton [package="[THT]"]
  R5 = Resistor [tolerance=±5% resistance=1k package=THT]
  R6 = Resistor [tolerance=±5% resistance=1k package=THT]
  R7 = Resistor [tolerance=±5% resistance=1k package=THT]
  R8 = Trimmer Potentiometer [maximum_resistance=10kΩ package=THT]
  R9 = Trimmer Potentiometer [maximum_resistance=10kΩ package=THT]
  R10 = Resistor [tolerance=±5% resistance=1k package=THT]
  Part2 = Logic Level Converter
  U1 = NodeMCU V1.0

nets:
  GND: Part1.GND, R1.leg2, R2.leg2, R5.Pin_1, R6.Pin_1, R7.Pin_1, R8.leg2, R9.leg2, R10.Pin_1, Part2.GND, U1.GND
  N1: Part1.D2, Part2.TX_HV
  N2: Part1.D3, S1.Pin_1, S1.Pin_2, R5.Pin_0
  N3: Part1.D4, Part2.RX_HV
  N4: Part1.D5, S2.Pin_1, S2.Pin_2, R6.Pin_0
  N5: Part1.D6, S3.Pin_1, S3.Pin_2, R7.Pin_0
  N6: Part1.D9, S4.Pin_1, S4.Pin_2, R10.Pin_0
  N7: Part1.5V, R1.leg1, R2.leg1, S1.Pin_3, S1.Pin_4, S2.Pin_3, S2.Pin_4, S3.Pin_3, S3.Pin_4, S4.Pin_3, S4.Pin_4, R8.leg1, R9.leg1, Part2.HV
  N8: Part1.A3, R1.wiper
  N9: Part1.A2, R2.wiper
  N10: Part1.A1, R8.wiper
  N11: Part1.A0, R9.wiper
  N12: Part2.LV, U1.3V3
  N13: Part2.RX_LV, U1.D2
  N14: Part2.TX_LV, U1.D4

notes:
  ANALOG PINS:
  A0-A0
  A1-A1
  A2-A2
  A3-A3
  DIGITAL PINS:
  D0-D3
  D1-D5
  D2-D6
  D3-D9
  SERIAL PINS:
  RX-D2
  TX-D4

custom parts:
  NodeMCU V1.0: ESP8266 based NodeMCU
