# Fritzing sketch SALIDAS (saved by Fritzing 0.9.3b)
breadboards: 2

parts:
  U2 = NodeMCU V1.0
  Part3 = Arduino Nano (Rev3.0)
  Part4 = Logic Level Converter
  LED1 = LED - 5mm [color="Red (633nm)" package="5 mm [THT]"]
  LED2 = LED - 5mm [color="Green (555nm)" package="5 mm [THT]"]
  LED3 = LED - 5mm [color="Blue (430nm)" package="5 mm [THT]"]
  LED4 = LED - 5mm [color="White (4500K)" package="5 mm [THT]"]
  LED5 = LED - 5mm [color="Green (555nm)" package="5 mm [THT]"]
  LED6 = LED - 5mm [color="Red (633nm)" package="5 mm [THT]"]
  LED7 = LED - 5mm [color="Blue (430nm)" package="5 mm [THT]"]
  LED8 = LED - 5mm [color="White (4500K)" package="5 mm [THT]"]
  R1 = Resistor [tolerance=±5% resistance=220 package=THT]
  R3 = Resistor [tolerance=±5% resistance=220 package=THT]  # not connected
  R4 = Resistor [tolerance=±5% resistance=220 package=THT]  # not connected
  R5 = Resistor [tolerance=±5% resistance=220 package=THT]
  R6 = Resistor [tolerance=±5% resistance=220 package=THT]
  R7 = Resistor [tolerance=±5% resistance=220 package=THT]
  R8 = Resistor [tolerance=±5% resistance=220 package=THT]
  R9 = Resistor [tolerance=±5% resistance=220 package=THT]
  R10 = Resistor [tolerance=±5% resistance=220 package=THT]
  R11 = Resistor [tolerance=±5% resistance=220 package=THT]

nets:
  N1: U2.D2, Part4.RX_LV
  N2: U2.D4, Part4.TX_LV
  N3: U2.3V3, Part4.LV
  GND: U2.GND, Part3.GND, Part4.GND, R1.Pin_1, R5.Pin_1, R6.Pin_1, R7.Pin_1, R8.Pin_0, R9.Pin_0, R10.Pin_0, R11.Pin_0
  N4: Part3.D2, Part4.TX_HV
  N5: Part3.D3, LED1.anode
  N6: Part3.D4, Part4.RX_HV
  N7: Part3.D5, LED2.anode
  N8: Part3.D6, Part3.5V, Part4.HV, LED3.anode
  N9: Part3.D9, LED4.anode
  N10: Part3.A3, LED8.anode
  N11: Part3.A2, LED7.anode
  N12: Part3.A1, LED5.anode
  N13: Part3.A0, LED6.anode
  N14: LED1.cathode, R8.Pin_1
  N15: LED2.cathode, R11.Pin_1
  N16: LED3.cathode, R9.Pin_1
  N17: LED4.cathode, R10.Pin_1
  N18: LED5.cathode, R5.Pin_0
  N19: LED6.cathode, R1.Pin_0
  N20: LED7.cathode, R6.Pin_0
  N21: LED8.cathode, R7.Pin_0

notes:
  ANALOG PINS:
  A0-D3
  A1-D5
  A2-D6
  A3-D9
  DIGITAL PINS:
  D0-A0
  D1-A1
  D2-A2
  D3-A3
  SERIAL PINS:
  RX-D2
  TX-D4

custom parts:
  NodeMCU V1.0: ESP8266 based NodeMCU
